# Fritzing sketch wemos_d1_R32_DHT22_LCD (saved by Fritzing 0.9.4)
breadboards: 1

parts:
  M1 = >Wemos D1 R32
  Part1 = DHT22 Breakout module [package="Breakout board"]
  Componente1 = LCD1602-I2C

nets:
  3V3: M1.3V3, M1.IO27, Part1.Out, Part1.+, Componente1.VCC
  GND: M1.GND, M1.IO12, M1.IO5, M1.IO23, M1.IO19, M1.IO18, M1.SDA, M1.SCL, Part1.-, Componente1.GND, Componente1.SDA, Componente1.SCL

custom parts:
  >Wemos D1 R32: Wemos D1 R32 - This board is used with dual-mode Wi-Fi and Bluetooth chips, which is safe, reliable, and scalable to a variety of applications. DC in 5V-12V, 1 analog input(3.2V max input), a Micro USB connection, Compatible with D1 R32=WiFi+bluetooth+UNO
  DHT22 Breakout module: DHT22 temperature and humidity sensor module, provides a low-latency serial interface to measure humidity and temperature.
  LCD1602-I2C: A standard character display, usually with 2x16 characters. Comes in many colors with LCM1602 IIC attached.
